# Fritzing sketch LightSynth (saved by Fritzing 0.9.0b)
breadboards: 2

parts:
  Part1 = Arduino Uno (Rev3) - ICSP
  R1 = Photocell (LDR) [package=THT]
  R2 = Photocell (LDR) [package=THT]
  R3 = Photocell (LDR) [package=THT]
  R4 = Photocell (LDR) [package=THT]
  R5 = Resistor [tolerance=±5% resistance=10k package=THT]
  R6 = Resistor [tolerance=±5% resistance=10k package=THT]
  R7 = Resistor [tolerance=±5% resistance=10k package=THT]
  R8 = Resistor [tolerance=±5% resistance=10k package=THT]

nets:
  N1: Part1.A0, R1.pin_0, R7.Pin_1
  N2: Part1.A1, R2.pin_0, R8.Pin_1
  N3: Part1.A2, R3.pin_1, R5.Pin_1
  N4: Part1.A3, R4.pin_1, R6.Pin_1
  N5: Part1.5V, R1.pin_1, R2.pin_1, R3.pin_0, R4.pin_0
  N6: Part1.GND, R5.Pin_0, R6.Pin_0, R7.Pin_0, R8.Pin_0
